# Fritzing sketch Schematic_V2 (saved by Fritzing 1.0.4)
breadboards: 1

parts:
  X1 = USB Connectors [package=usb-minib-nostop]
  A2 = MX1508
  A1 = ENS160 AHT21
  S1 = Toggle Switch [package=THT]
  F1 = Fan - 4 wire [package=THT]
  Part1 = Arduino Nano (Rev3.0)
  Squix1 = OLED 0.96" 128x64 I2C SSD1306

nets:
  GND: X1.GND, A2.Pin_2, A1.Pin_3, Part1.GND, Squix1.GND
  N1: X1.VBUS, A2.Pin_1, S1.COM
  N2: A2.Pin_3, Part1.D3
  N3: A2.Pin_4, Part1.D2
  N4: A2.Pin_9, F1.GND
  N5: A2.Pin_10, F1.Power
  5V: A1.Pin_1, Part1.5V, Squix1.VCC
  N6: A1.Pin_4, Part1.A5, Squix1.SCL
  N7: A1.Pin_5, Part1.A4, Squix1.SCA
  N8: S1.L1, Part1.VIN

notes:
  5V Arduino
  V_in (5v-12v)

custom parts:
  MX1508: MX1508 DC Motor Driver is a low-cost motor driver module that can control DC stepper motors of current rating up to 2A.
  ENS160 AHT21: The CO2 Gas- Air- Sensor is based on ENS160 in combination with an AHT21 Temperature Humidity Sensor.
  Fan - 4 wire: Fan, 4 wire with tach.
